// Logisim project lab1.5.circ as structural Verilog: 2 circuits, main circuit 4-1MUX
module main (
  input  D0,
  input  D1,
  input  S,
  output Y
);

  wire transistor_1_out;

  Transistor transistor_1 (.in(1'b1), .out(transistor_1_out), .gate(S));
  Transistor #(.\type ("n")) transistor_2 (.in(1'b0), .out(transistor_1_out), .gate(S));
  // Transmission_Gate transmission_1: pin names not known; wires that end beside it: D0, S, transistor_1_out, Y
  // Transmission_Gate transmission_2: pin names not known; wires that end beside it: 1'b0, D1, transistor_1_out, S, Y

  // Notes on the sheet:
  //   输入引脚
  //   请勿修改引脚名称及电路封装外观
  //   提示：使用传输门和晶体管来实现二选一多路选择器，禁止直接使用选择器组件。
  //   输出引脚
endmodule

module _4_1MUX (
  input  D0,
  input  D1,
  input  in_3,
  input  in_4,
  input  S0,
  input  in_6,
  output out_7
);

  wire main_1_y, main_2_y;

  main main_1 (.D0(D0), .D1(D1), .S(S0), .Y(main_1_y));
  main main_2 (.D0(in_3), .D1(in_4), .S(S0), .Y(main_2_y));
  main main_3 (.D0(main_1_y), .D1(main_2_y), .S(in_6), .Y(out_7));
endmodule
