// Logisim project 思考题1-带标志加法器.circ as structural Verilog: 2 circuits, main circuit main
module main (
  input  [3:0] X,
  input  [3:0] Y,
  input  Cin,
  output [3:0] F,
  output Cout,
  output CF,
  output ZF,
  output SF,
  output OF
);

  wire FA0_cout, FA1_cout, FA2_cout, multiplexer_1_out, multiplexer_2_out, multiplexer_3_out,
       multiplexer_4_out;
  wire [3:0] not_1_out;

  Hex_Digit_Display hex_digit_display_1 ();  // open: value, dp
  Hex_Digit_Display hex_digit_display_2 ();  // open: value, dp
  assign not_1_out = ~Y;  // NOT_Gate not_1, 4 bits wide
  Hex_Digit_Display hex_digit_display_3 ();  // open: value, dp
  FA FA0 (.A(X[0]), .B(multiplexer_1_out), .Cin(Cin), .Cout(FA0_cout), .F(F[0]));
  Multiplexer #(.enable("false")) multiplexer_1 (.in0(Y[0]), .in1(not_1_out[0]), .out(multiplexer_1_out), .sel(Cin));
  Multiplexer #(.enable("false")) multiplexer_2 (.in0(Y[1]), .in1(not_1_out[1]), .out(multiplexer_2_out), .sel(Cin));
  Multiplexer #(.enable("false")) multiplexer_3 (.in0(Y[2]), .in1(not_1_out[2]), .out(multiplexer_3_out), .sel(Cin));
  Multiplexer #(.enable("false")) multiplexer_4 (.in0(Y[3]), .in1(not_1_out[3]), .out(multiplexer_4_out), .sel(Cin));
  xor xor_1 (CF, Cin, Cout);
  FA FA1 (.A(X[1]), .B(multiplexer_2_out), .Cin(FA0_cout), .Cout(FA1_cout), .F(F[1]));
  FA FA2 (.A(X[2]), .B(multiplexer_3_out), .Cin(FA1_cout), .Cout(FA2_cout), .F(F[2]));
  FA FA3 (.A(X[3]), .B(multiplexer_4_out), .Cin(FA2_cout), .Cout(Cout), .F(F[3]));
  xor xor_2 (OF, FA2_cout, Cout);
  nor nor_1 (ZF, F[0], F[1], F[2], F[3]);

  assign SF = F[3];

  // Other names for the same wires on the sheet: SUM[3:0] = F; 操作数x[3:0] = X; 操作数y[3:0] = Y

  // Notes on the sheet:
  //   +
  //   输入引脚
  //   =
  //   请勿修改引脚名称、电路名称及电路封装外观
  //   提示：使用独立逻辑门及全加器FA子电路实现4位二进制数加减法器，禁止直接使用加减法器组件。
  //   输出引脚
endmodule

module FA (
  input  A,
  input  B,
  input  Cin,
  output F,
  output Cout
);

  wire and_1_out, and_2_out, and_3_out, xor_1_out;

  xor xor_1 (xor_1_out, A, B);
  and and_1 (and_1_out, A, B);
  and and_2 (and_2_out, B, Cin);
  and and_3 (and_3_out, A, Cin);
  xor xor_2 (F, xor_1_out, Cin);
  or or_1 (Cout, and_1_out, and_2_out, and_3_out);

  // Notes on the sheet:
  //   全加器
endmodule
