// Logisim project lab3.2.circ as structural Verilog: 2 circuits, main circuit SHRG4U
module SHRG4U (
  input  CLK,
  input  CLR_L,
  input  RIN,
  input  D3,
  input  D2,
  input  D1,
  input  D0,
  input  LIN,
  input  S1,
  input  S0,
  output Q3,
  output Q2,
  output Q1,
  output Q0
);

  wire _00_2_out, _00_3_out, _00_4_out, _00_out, _01_2_out, _01_3_out, _01_4_out, _01_out, _10_2_out,
       _10_3_out, _10_4_out, _10_out, _11_2_out, _11_3_out, _11_4_out, _11_out, not_1_out, not_2_out,
       not_3_out, not_4_out, not_5_out, not_6_out, or_1_out, or_2_out, or_3_out, or_4_out;

  not not_1 (not_1_out, S1);
  not not_2 (not_2_out, S0);
  not not_3 (not_3_out, CLK);
  not not_4 (not_4_out, CLR_L);
  not not_5 (not_5_out, not_1_out);
  not not_6 (not_6_out, not_2_out);
  and _10 (_10_out, RIN, not_5_out, not_2_out);
  and _00 (_00_out, Q3, not_1_out, not_2_out);
  and _11 (_11_out, D3, not_5_out, not_6_out);
  and _01 (_01_out, Q2, not_1_out, not_6_out);
  and _10_2 (_10_2_out, Q3, not_5_out, not_2_out);
  and _00_2 (_00_2_out, Q2, not_1_out, not_2_out);
  and _11_2 (_11_2_out, D2, not_5_out, not_6_out);
  and _01_2 (_01_2_out, Q1, not_1_out, not_6_out);
  and _10_3 (_10_3_out, Q2, not_5_out, not_2_out);
  and _00_3 (_00_3_out, Q1, not_1_out, not_2_out);
  and _11_3 (_11_3_out, D1, not_5_out, not_6_out);
  and _01_3 (_01_3_out, Q0, not_1_out, not_6_out);
  and _10_4 (_10_4_out, Q1, not_5_out, not_2_out);
  and _00_4 (_00_4_out, Q0, not_1_out, not_2_out);
  and _11_4 (_11_4_out, D0, not_5_out, not_6_out);
  and _01_4 (_01_4_out, LIN, not_1_out, not_6_out);
  or or_1 (or_1_out, _10_out, _00_out, _11_out, _01_out);
  or or_2 (or_2_out, _10_2_out, _00_2_out, _11_2_out, _01_2_out);
  or or_3 (or_3_out, _10_3_out, _00_3_out, _11_3_out, _01_3_out);
  or or_4 (or_4_out, _10_4_out, _00_4_out, _11_4_out, _01_4_out);
  D_Flip_Flop #(.trigger("falling")) QD (.clk(not_3_out), .D(or_1_out), .Q(Q3), .reset(not_4_out));  // open: Qn, preset
  D_Flip_Flop #(.trigger("falling")) QC (.clk(not_3_out), .D(or_2_out), .Q(Q2), .reset(not_4_out));  // open: Qn, preset
  D_Flip_Flop #(.trigger("falling")) QB (.clk(not_3_out), .D(or_3_out), .Q(Q1), .reset(not_4_out));  // open: Qn, preset
  D_Flip_Flop #(.trigger("falling")) QA (.clk(not_3_out), .D(or_4_out), .Q(Q0), .reset(not_4_out));  // open: Qn, preset

  // Notes on the sheet:
  //   输入引脚
  //   请勿修改引脚名称、电路名称及电路封装外观
  //   提示：使用独立逻辑门实现4位异步清零移位寄存器，禁止直接使用移位寄存器组件。
  //   输出引脚
endmodule

module \伪随机数  (
  input  CLR,
  input  CLR_2,
  input  S1,
  input  S1_2,
  input  S0,
  input  S0_2
);

  wire clock_1_out, clock_2_out, xor_1_out, xor_2_out, xor_3_out, xor_4_out;
  wire [3:0] shrg4u_1_q3, shrg4u_2_q3, shrg4u_3_q3;
  wire [3:1] shrg4u_4_q2;

  Clock clock_1 (.out(clock_1_out));
  SHRG4U shrg4u_1 (
    .CLK(clock_1_out), .CLR_L(CLR_2), .RIN(xor_1_out), .Q3(shrg4u_1_q3[0]), .Q2(shrg4u_1_q3[1]), .D3(1'b0),
    .D2(1'b1), .D1(1'b0), .Q1(shrg4u_1_q3[2]), .Q0(shrg4u_1_q3[3]), .D0(1'b0), .S1(S1_2), .S0(S0_2));  // open: LIN
  xor xor_1 (xor_1_out, shrg4u_1_q3[3], shrg4u_1_q3[2]);
  SHRG4U shrg4u_2 (
    .CLK(clock_1_out), .CLR_L(CLR_2), .RIN(xor_2_out), .Q3(shrg4u_2_q3[0]), .Q2(shrg4u_2_q3[1]), .D3(1'b0),
    .D2(1'b1), .D1(1'b0), .Q1(shrg4u_2_q3[2]), .Q0(shrg4u_2_q3[3]), .D0(1'b0), .S1(S1_2), .S0(S0_2));  // open: LIN
  xor xor_2 (xor_2_out, shrg4u_2_q3[0], shrg4u_2_q3[3]);
  Hex_Digit_Display hex_digit_display_1 (.value(shrg4u_1_q3));  // open: dp
  Hex_Digit_Display hex_digit_display_2 (.value(shrg4u_2_q3));  // open: dp
  Clock clock_2 (.out(clock_2_out));
  SHRG4U shrg4u_3 (
    .CLK(clock_2_out), .CLR_L(CLR), .RIN(xor_3_out), .Q3(shrg4u_3_q3[0]), .Q2(shrg4u_3_q3[1]), .D3(1'b0),
    .D2(1'b1), .D1(1'b0), .Q1(shrg4u_3_q3[2]), .Q0(shrg4u_3_q3[3]), .D0(1'b0), .S1(S1), .S0(S0));  // open: LIN
  xor xor_3 (xor_3_out, shrg4u_3_q3[3], shrg4u_3_q3[2]);
  Hex_Digit_Display hex_digit_display_3 (.value(shrg4u_3_q3));  // open: dp
  xor xor_4 (xor_4_out, shrg4u_4_q2[2], shrg4u_4_q2[3]);
  SHRG4U shrg4u_4 (
    .CLK(clock_2_out), .CLR_L(CLR), .RIN(xor_4_out), .Q3(shrg4u_4_q2[2]), .Q2(shrg4u_4_q2[1]),
    .D3(shrg4u_3_q3[0]), .D2(shrg4u_3_q3[1]), .D1(shrg4u_3_q3[2]), .Q1(shrg4u_4_q2[2]), .Q0(shrg4u_4_q2[3]),
    .D0(shrg4u_3_q3[3]), .S1(S1), .S0(S0));  // open: LIN
  Hex_Digit_Display hex_digit_display_4 (.value({shrg4u_4_q2, shrg4u_4_q2[2]}));  // open: dp
endmodule
