// Logisim project lab3.5.circ as structural Verilog: 1 circuit, main circuit main
module main (
  input  CLK,
  input  LD,
  input  [3:0] HH1,
  input  [3:0] HH0,
  input  [3:0] MM1,
  input  [3:0] MM0,
  input  [3:0] SS1,
  input  [3:0] SS0,
  input  [3:0] \时高位 ,
  input  [3:0] \时低位 ,
  input  [3:0] \分高位 ,
  input  [3:0] \分低位 ,
  input  [3:0] \秒高位 ,
  input  [3:0] \秒低位 ,
  output [3:0] HH_H,
  output [3:0] HH_L,
  output [3:0] MM_H,
  output [3:0] MM_L,
  output [3:0] SS_H,
  output [3:0] SS_L,
  output LED_R,
  output LED_G,
  output LED_B,
  output out_24,
  output INErr
);

  wire and_1_out, and_2_out, and_3_out, and_4_out, and_5_out, and_6_out, and_7_out, and_8_out, and_9_out,
       and_10_out, and_11_out, and_12_out, and_14_out, and_16_out, and_17_out, and_18_out, and_19_out,
       and_20_out, cntr4u_4_q0, cntr4u_4_q1, cntr4u_5_q0, cntr4u_5_q1, cntr4u_5_q2, cntr4u_5_q3,
       comparator_1_eq, comparator_2_eq, comparator_3_eq, comparator_4_eq, comparator_5_eq, comparator_6_eq,
       decoder_1_out0, decoder_1_out1, decoder_1_out2, decoder_1_out3, decoder_1_out4, decoder_1_out5,
       decoder_2_out0, decoder_2_out1, decoder_2_out2, decoder_3_out0, decoder_3_out1, decoder_3_out2,
       decoder_3_out3, decoder_4_out0, decoder_4_out1, decoder_4_out2, decoder_4_out3, decoder_4_out4,
       decoder_4_out5, not_1_out, not_2_out, not_3_out, or_1_out, or_2_out, or_3_out, or_4_out, or_5_out,
       or_6_out, or_7_out, or_8_out, or_9_out, STOP, \闹钟启动 ;

  and and_1 (and_1_out, LD, not_1_out);
  not not_1 (not_1_out, INErr);
  or or_1 (or_1_out, decoder_1_out0, decoder_1_out1, decoder_1_out2, decoder_1_out3, decoder_1_out4, decoder_1_out5);
  Decoder #(.select(4), .enable("false")) decoder_1 (
    .out0(decoder_1_out0), .out1(decoder_1_out1), .out2(decoder_1_out2), .out3(decoder_1_out3),
    .out4(decoder_1_out4), .out5(decoder_1_out5), .sel(MM1));  // open: out6, out7, out8, out9, out10, out11, out12, out13, out14, out15
  and and_2 (and_2_out, or_5_out, out_24);
  and and_3 (and_3_out, and_6_out, and_14_out);
  Decoder #(.select(4), .enable("false")) decoder_2 (
    .out0(decoder_2_out0), .out1(decoder_2_out1), .out2(decoder_2_out2), .sel(HH1));  // open: out3, out4, out5, out6, out7, out8, out9, out10, out11, out12, out13, out14, out15
  or or_2 (or_2_out, decoder_2_out1, decoder_2_out0);
  or or_3 (or_3_out, decoder_3_out0, decoder_3_out1, decoder_3_out2, decoder_3_out3);
  Decoder #(.select(4), .enable("false")) decoder_3 (
    .out0(decoder_3_out0), .out1(decoder_3_out1), .out2(decoder_3_out2), .out3(decoder_3_out3), .sel(HH0));  // open: out4, out5, out6, out7, out8, out9, out10, out11, out12, out13, out14, out15
  or or_4 (or_4_out, decoder_4_out0, decoder_4_out1, decoder_4_out2, decoder_4_out3, decoder_4_out4, decoder_4_out5);
  Decoder #(.select(4), .enable("false")) decoder_4 (
    .out0(decoder_4_out0), .out1(decoder_4_out1), .out2(decoder_4_out2), .out3(decoder_4_out3),
    .out4(decoder_4_out4), .out5(decoder_4_out5), .sel(SS1));  // open: out6, out7, out8, out9, out10, out11, out12, out13, out14, out15
  and and_4 (and_4_out, HH_H[1], and_9_out);
  or or_5 (or_5_out, and_4_out, and_5_out);
  and and_5 (and_5_out, HH_L[0], HH_L[3]);
  CNTR4U cntr4u_1 (
    .CLK(CLK), .LD(and_1_out), .CLR(and_2_out), .Q0(HH_L[0]), .Q1(HH_L[1]), .D0(HH0[0]), .D1(HH0[1]),
    .D2(HH0[2]), .Q2(HH_L[2]), .Q3(HH_L[3]), .D3(HH0[3]), .ENP(out_24), .ENT(out_24));  // open: RCO
  and and_6 (and_6_out, MM_L[0], MM_L[3]);
  CNTR4U cntr4u_2 (
    .CLK(CLK), .LD(and_1_out), .CLR(and_3_out), .Q0(MM_L[0]), .Q1(MM_L[1]), .D0(MM0[0]), .D1(MM0[1]),
    .D2(MM0[2]), .Q2(MM_L[2]), .Q3(MM_L[3]), .D3(MM0[3]), .ENP(and_14_out), .ENT(and_14_out));  // open: RCO
  and and_7 (and_7_out, SS_L[0], SS_L[3]);
  CNTR4U cntr4u_3 (
    .CLK(CLK), .LD(and_1_out), .CLR(and_7_out), .Q0(SS_L[0]), .Q1(SS_L[1]), .D0(SS0[0]), .D1(SS0[1]),
    .D2(SS0[2]), .Q2(SS_L[2]), .Q3(SS_L[3]), .D3(SS0[3]), .ENP(1'b1), .ENT(1'b1));  // open: RCO
  and and_8 (and_8_out, decoder_2_out2, or_3_out);
  Hex_Digit_Display hex_digit_display_1 (.value(HH_H));  // open: dp
  and and_9 (and_9_out, HH_L[0], HH_L[1]);
  or or_6 (or_6_out, out_24, or_9_out);
  or or_7 (or_7_out, out_24, or_9_out);
  Hex_Digit_Display hex_digit_display_2 (.value(MM_H));  // open: dp
  Hex_Digit_Display hex_digit_display_3 (.value(HH_L), .dp(1'b1));
  or or_8 (or_8_out, and_8_out, or_2_out);
  CNTR4U cntr4u_4 (
    .CLK(CLK), .LD(1'b0), .CLR(STOP), .Q0(cntr4u_4_q0), .Q1(cntr4u_4_q1), .Q2(LED_B), .ENP(or_6_out),
    .ENT(or_6_out));  // open: D0, D1, D2, Q3, D3, RCO
  CNTR4U cntr4u_5 (
    .CLK(CLK), .LD(out_24), .CLR(STOP), .Q0(cntr4u_5_q0), .Q1(cntr4u_5_q1), .D0(1'b0), .D1(1'b1), .D2(1'b1),
    .Q2(cntr4u_5_q2), .Q3(cntr4u_5_q3), .D3(1'b0), .ENP(or_7_out), .ENT(or_7_out), .RCO(STOP));
  Hex_Digit_Display hex_digit_display_4 (.value(SS_H));  // open: dp
  Hex_Digit_Display hex_digit_display_5 (.value(MM_L), .dp(1'b1));
  not not_2 (not_2_out, INErr);
  not not_3 (not_3_out, and_10_out);
  and and_10 (and_10_out, or_8_out, or_1_out, or_4_out);
  xor xor_1 (LED_R, cntr4u_4_q0, cntr4u_4_q1);
  xor xor_2 (LED_G, cntr4u_4_q1, LED_B);
  or or_9 (or_9_out, cntr4u_5_q3, cntr4u_5_q2, cntr4u_5_q1, cntr4u_5_q0);
  Hex_Digit_Display hex_digit_display_6 (.value(SS_L), .dp(1'b1));
  and and_11 (and_11_out, LD, not_2_out);
  and and_12 (and_12_out, HH_H[1], and_2_out);
  and and_13 (out_24, and_16_out, and_3_out);
  and and_14 (and_14_out, and_17_out, and_7_out);
  and and_15 (INErr, LD, not_3_out);
  CNTR4U cntr4u_6 (
    .CLK(CLK), .LD(and_11_out), .CLR(and_12_out), .Q0(HH_H[0]), .Q1(HH_H[1]), .D0(HH1[0]), .D1(HH1[1]),
    .D2(HH1[2]), .Q2(HH_H[2]), .Q3(HH_H[3]), .D3(HH1[3]), .ENP(and_5_out), .ENT(and_5_out));  // open: RCO
  CNTR4U cntr4u_7 (
    .CLK(CLK), .LD(and_11_out), .CLR(out_24), .Q0(MM_H[0]), .Q1(MM_H[1]), .D0(MM1[0]), .D1(MM1[1]),
    .D2(MM1[2]), .Q2(MM_H[2]), .Q3(MM_H[3]), .D3(MM1[3]), .ENP(and_3_out), .ENT(and_3_out));  // open: RCO
  CNTR4U cntr4u_8 (
    .CLK(CLK), .LD(and_11_out), .CLR(and_14_out), .Q0(SS_H[0]), .Q1(SS_H[1]), .D0(SS1[0]), .D1(SS1[1]),
    .D2(SS1[2]), .Q2(SS_H[2]), .Q3(SS_H[3]), .D3(SS1[3]), .ENP(and_7_out), .ENT(and_7_out));  // open: RCO
  and and_16 (and_16_out, MM_H[0], MM_H[2]);
  and and_17 (and_17_out, SS_H[0], SS_H[2]);
  // RGBLed RGBLED: pin names not known; wires that end beside it: LED_R, LED_G, LED_B
  Comparator #(.width(4)) comparator_1 (.a(\时高位 ), .b(HH_H), .eq(comparator_1_eq));  // open: gt, lt
  Comparator #(.width(4)) comparator_2 (.a(\时低位 ), .b(HH_L), .eq(comparator_2_eq));  // open: gt, lt
  Comparator #(.width(4)) comparator_3 (.a(\分高位 ), .b(MM_H), .eq(comparator_3_eq));  // open: gt, lt
  Comparator #(.width(4)) comparator_4 (.a(\分低位 ), .b(MM_L), .eq(comparator_4_eq));  // open: gt, lt
  Comparator #(.width(4)) comparator_5 (.a(\秒高位 ), .b(SS_H), .eq(comparator_5_eq));  // open: gt, lt
  Comparator #(.width(4)) comparator_6 (.a(\秒低位 ), .b(SS_L), .eq(comparator_6_eq));  // open: gt, lt
  // Buzzer buzzer_1: pin names not known; wires that end beside it: \闹钟启动 
  and and_18 (and_18_out, comparator_1_eq, comparator_2_eq);
  and and_19 (and_19_out, comparator_3_eq, comparator_4_eq);
  and and_20 (and_20_out, comparator_5_eq, comparator_6_eq);
  and and_21 (\闹钟启动 , and_18_out, and_19_out, and_20_out);

  // Other names for the same wires on the sheet: H0[3:0] = HH_L; H1[3:0] = HH_H; M0[3:0] = MM_L; M1[3:0] = MM_H;
  //   S0[3:0] = SS_L; S1[3:0] = SS_H; LED_EN = out_24; START = out_24; 闹H0[3:0] = \时低位 ; 闹H1[3:0] = \时高位 ;
  //   闹M0[3:0] = \分低位 ; 闹M1[3:0] = \分高位 ; 闹S0[3:0] = \秒低位 ; 闹S1[3:0] = \秒高位 

  // Notes on the sheet:
  //   设置初始时间BCD码
  //   输入信号
  //   请勿修改引脚名称、电路名称及电路封装外观
  //   数字时钟
  //   提示：使用4位二进制加法计数器子电路、比较器和独立逻辑门组件实现数字时钟。
  //   在载入有效时，检测设置数据错误
  //   生成三色LED显示信号，持续10个时钟周期
endmodule
