// Logisim project 快速乘法器-4位示意.circ as structural Verilog: 3 circuits, main circuit ADDER4b
module ADDER4b (
  input  [3:0] X,
  input  [3:0] Y,
  input  Cin,
  output [3:0] F,
  output Cout
);

  wire fa_1_cout, fa_2_cout, fa_3_cout;
  wire [3:0] bit_extender_1_out, xor_1_out;

  assign bit_extender_1_out = {{3{Cin}}, Cin};  // Bit_Extender bit_extender_1
  Hex_Digit_Display hex_digit_display_1 (.value(X), .dp(1'b0));
  assign xor_1_out = bit_extender_1_out ^ Y;  // XOR_Gate xor_1, 4 bits wide
  Hex_Digit_Display hex_digit_display_2 (.value(xor_1_out), .dp(1'b0));
  FA fa_1 (.A(X[0]), .B(xor_1_out[0]), .Cin(Cin), .F(F[0]), .Cout(fa_1_cout));
  Hex_Digit_Display hex_digit_display_3 (.value(F), .dp(1'b0));
  FA fa_2 (.A(X[1]), .B(xor_1_out[1]), .Cin(fa_1_cout), .F(F[1]), .Cout(fa_2_cout));
  FA fa_3 (.A(X[2]), .B(xor_1_out[2]), .Cin(fa_2_cout), .F(F[2]), .Cout(fa_3_cout));
  FA fa_4 (.A(X[3]), .B(xor_1_out[3]), .Cin(fa_3_cout), .F(F[3]), .Cout(Cout));

  // Other names for the same wires on the sheet: SUM[3:0] = F; 操作数x[3:0] = X; 操作数y[3:0] = Y

  // Notes on the sheet:
  //   输入引脚
  //   +
  //   =
  //   请勿修改引脚名称、电路名称及电路封装外观
  //   提示：使用独立逻辑门及全加器FA子电路实现4位二进制数加减法器，禁止直接使用加减法器组件。
  //   输出引脚
endmodule

module FA (
  input  A,
  input  B,
  input  Cin,
  output F,
  output Cout
);

  wire and_1_out, and_2_out, and_3_out;

  xor xor_1 (F, A, B, Cin);
  and and_1 (and_1_out, A, B);
  and and_2 (and_2_out, B, Cin);
  and and_3 (and_3_out, A, Cin);
  or or_1 (Cout, and_1_out, and_2_out, and_3_out);

  // Notes on the sheet:
  //   全加器
endmodule

module \快速乘法器  (
  input  [3:0] Y,
  input  [3:0] X,
  output [7:0] out_3
);

  wire [3:0] adder4b_2_f, adder4b_3_f, adder4b_4_cout, multiplexer_1_out, multiplexer_2_out,
       multiplexer_3_out, multiplexer_4_out;

  Multiplexer #(.width(4), .enable("false")) multiplexer_1 (
    .in0(4'b0000), .in1(X), .out(multiplexer_1_out), .sel(Y[0]));
  Multiplexer #(.width(4), .enable("false")) multiplexer_2 (
    .in0(4'b0000), .in1(X), .out(multiplexer_2_out), .sel(Y[1]));
  Multiplexer #(.width(4), .enable("false")) multiplexer_3 (
    .in0(4'b0000), .in1(X), .out(multiplexer_3_out), .sel(Y[2]));
  Multiplexer #(.width(4), .enable("false")) multiplexer_4 (
    .in0(4'b0000), .in1(X), .out(multiplexer_4_out), .sel(Y[3]));
  ADDER4b adder4b_1 (.X(adder4b_3_f), .Y(multiplexer_4_out), .F(out_3[6:3]), .Cout(out_3[7]), .Cin(1'b0));
  ADDER4b adder4b_2 (
    .X(adder4b_4_cout), .Y(multiplexer_2_out), .F({adder4b_2_f[2:0], out_3[1]}), .Cout(adder4b_2_f[3]),
    .Cin(1'b0));
  ADDER4b adder4b_3 (
    .X(adder4b_2_f), .Y(multiplexer_3_out), .F({adder4b_3_f[2:0], out_3[2]}), .Cout(adder4b_3_f[3]),
    .Cin(1'b0));
  ADDER4b adder4b_4 (
    .X(4'b0000), .Y(multiplexer_1_out), .F({adder4b_4_cout[2:0], out_3[0]}), .Cout(adder4b_4_cout[3]),
    .Cin(1'b0));

  // Other names for the same wires on the sheet: tunnel[7:0] = out_3
endmodule
