// Logisim project lab5.2.circ as structural Verilog: 1 circuit, main circuit DataRam
// DataRAM
module DataRam (
  input  CLK,
  input  CLR,
  input  WE,
  input  [2:0] MemOp,
  input  [17:0] Addr,
  input  [31:0] Din,
  output AlignErr,
  output [31:0] DataOut
);

  wire \_1位 , \_2位 , \_4位 , and_1_out, and_2_out, and_3_out, and_4_out, and_5_out, and_6_out, and_7_out,
       and_8_out, and_10_out, and_11_out, and_13_out, and_14_out, nor_1_out, or_1_out, SEL0, SEL1, SEL2,
       SEL3, \写入 ;
  wire [7:0] multiplexer_1_out, multiplexer_2_out, multiplexer_3_out, multiplexer_4_out;
  wire [15:0] multiplexer_5_out;
  wire [31:0] bit_extender_1_out, bit_extender_2_out, bit_extender_3_out, bit_extender_4_out, \低8位_data ;

  Multiplexer #(.width(8), .enable("false")) multiplexer_1 (
    .in0(Din[7:0]), .in1(Din[15:8]), .out(multiplexer_1_out), .sel(SEL0));
  Multiplexer #(.width(8), .enable("false")) multiplexer_2 (
    .in0(Din[7:0]), .in1(Din[23:16]), .out(multiplexer_2_out), .sel(SEL0));
  Multiplexer #(.select(2), .width(8), .enable("false")) multiplexer_3 (
    .in0(Din[7:0]), .in2(Din[15:8]), .in3(Din[31:24]), .out(multiplexer_3_out), .sel({SEL2, SEL0}));  // open: in1
  and and_1 (and_1_out, WE, \写入 );
  and and_2 (and_2_out, \_4位 , ~Addr[0], ~Addr[1]);  // AND_Gate
  and and_3 (and_3_out, \_1位 , Addr[0], Addr[1]);
  and and_4 (and_4_out, \_2位 , ~Addr[0], Addr[1]);  // AND_Gate
  and and_5 (and_5_out, \_1位 , ~Addr[0], Addr[1]);  // AND_Gate
  and and_6 (and_6_out, \_1位 , Addr[0], ~Addr[1]);  // AND_Gate
  and and_7 (and_7_out, \_2位 , ~Addr[0], ~Addr[1]);  // AND_Gate
  and and_8 (and_8_out, \_1位 , ~Addr[0], ~Addr[1]);  // AND_Gate
  nor nor_1 (nor_1_out, \_1位 , \_4位 , \_2位 );
  or or_1 (or_1_out, Addr[0], Addr[1]);
  and and_9 (\_1位 , MemOp[0], ~MemOp[1]);  // AND_Gate
  or or_2 (SEL3, and_2_out, and_3_out, and_4_out);
  or or_3 (SEL2, and_2_out, and_5_out, and_4_out);
  or or_4 (SEL1, and_2_out, and_6_out, and_7_out);
  or or_5 (SEL0, and_2_out, and_8_out, and_7_out);
  and and_10 (and_10_out, \_2位 , Addr[0]);
  and and_11 (and_11_out, \_4位 , or_1_out);
  and and_12 (\_2位 , ~MemOp[0], MemOp[1]);  // AND_Gate
  nor nor_2 (\_4位 , MemOp[0], MemOp[1], MemOp[2]);
  and and_13 (and_13_out, MemOp[0], ~MemOp[1], MemOp[2]);  // AND_Gate
  and and_14 (and_14_out, ~MemOp[0], MemOp[1], MemOp[2]);  // AND_Gate
  or or_6 (AlignErr, and_10_out, nor_1_out, and_11_out);
  or or_7 (\写入 , \_4位 , and_13_out, and_14_out);
  RAM #(.addrWidth(16), .bus("separate"), .Select("high"), .simpleMode("false")) \u_低8位  (
    .addr(Addr[17:2]), .din(Din[7:0]), .data(\低8位_data [7:0]), .str(and_1_out), .sel(SEL0), .clk(CLK),
    .clr(CLR));  // open: ld
  RAM #(.addrWidth(16), .bus("separate"), .Select("high"), .simpleMode("false")) ram_1 (
    .addr(Addr[17:2]), .din(multiplexer_1_out), .data(\低8位_data [15:8]), .str(and_1_out), .sel(SEL1),
    .clk(CLK), .clr(CLR));  // open: ld
  RAM #(.addrWidth(16), .bus("separate"), .Select("high"), .simpleMode("false")) ram_2 (
    .addr(Addr[17:2]), .din(multiplexer_2_out), .data(\低8位_data [23:16]), .str(and_1_out), .sel(SEL2),
    .clk(CLK), .clr(CLR));  // open: ld
  RAM #(.addrWidth(16), .bus("separate"), .Select("high"), .simpleMode("false")) \u_高8位  (
    .addr(Addr[17:2]), .din(multiplexer_3_out), .data(\低8位_data [31:24]), .str(and_1_out), .sel(SEL3),
    .clk(CLK), .clr(CLR));  // open: ld
  Multiplexer #(.select(2), .width(8), .enable("false")) multiplexer_4 (
    .in0(\低8位_data [7:0]), .in1(\低8位_data [15:8]), .in2(\低8位_data [23:16]), .in3(\低8位_data [31:24]),
    .out(multiplexer_4_out), .sel(Addr[1:0]));
  Multiplexer #(.select(2), .width(16), .enable("false")) multiplexer_5 (
    .in0(\低8位_data [15:0]), .in2(\低8位_data [31:16]), .out(multiplexer_5_out), .sel(Addr[1:0]));  // open: in1, in3
  assign bit_extender_1_out = {{24{1'b0}}, multiplexer_4_out};  // Bit_Extender bit_extender_1
  assign bit_extender_2_out = {{16{1'b0}}, multiplexer_5_out};  // Bit_Extender bit_extender_2
  assign bit_extender_3_out = {{24{multiplexer_4_out[7]}}, multiplexer_4_out};  // Bit_Extender bit_extender_3
  assign bit_extender_4_out = {{16{multiplexer_5_out[15]}}, multiplexer_5_out};  // Bit_Extender bit_extender_4
  Multiplexer #(.select(3), .width(32), .enable("false")) multiplexer_6 (
    .in0(\低8位_data ), .in1(bit_extender_1_out), .in2(bit_extender_2_out), .in5(bit_extender_3_out),
    .in6(bit_extender_4_out), .out(DataOut), .sel(MemOp));  // open: in3, in4, in7

  // Other names for the same wires on the sheet: addr2[1:0] = Addr[1:0]; Dout[31:0] = DataOut

  // Notes on the sheet:
  //   输入引脚
  //   请勿修改引脚名称、电路名称及电路封装外观
  //   为了后续实验中的引用，不要修改MemOp的编码定义、引脚名称和在布局中的位置。
  //   32位数据存储器，按字节分4片存储，可按照字节、半字和字进行存储；读取字节或半字时，支持0扩展和符号位扩展。
  //   输出引脚
endmodule
