// Logisim project lab5.5.circ as structural Verilog: 15 circuits, main circuit main
module main (
  input  [2:0] ExtOp,
  input  [2:0] MemOp,
  input  RegWr,
  input  ALUASrc,
  input  MemWr,
  input  [1:0] ALUBSrc,
  input  [31:0] Initial_Address,
  input  [3:0] ALUctr,
  input  MemtoReg,
  input  [2:0] BandJ,
  input  clk,
  input  ReSet,
  output [31:0] PC,
  output [31:0] BusW,
  output [31:0] Din,
  output NPCASrc,
  output NPCBSrc
);

  wire alu_1_zero;
  wire [31:0] alu_1_s, dataram_1_dataout, idu_1_busa, idu_1_dataa, idu_1_datab, idu_1_imm, rom_1_data;

  ROM #(.addrWidth(16), .dataWidth(32), .Select("high")) rom_1 (.addr(PC[17:2]), .data(rom_1_data), .sel(1'b1));
  IDU idu_1 (
    .ExtOp(ExtOp), .RegWr(RegWr), .Imm(idu_1_imm), .ALUASrc(ALUASrc), .ALUBSrc(ALUBSrc), .CLK(clk),
    .IR(rom_1_data), .BusW(BusW), .PC(PC), .DataA(idu_1_dataa), .DataB(idu_1_datab), .BusA(idu_1_busa),
    .BusB(Din));  // open: OpCode, Funct3, Funct7
  ALU alu_1 (.A(idu_1_dataa), .B(idu_1_datab), .ALUctr(ALUctr), .S(alu_1_s), .Zero(alu_1_zero));
  IFU ifu_1 (
    .CLK(clk), .Reset(ReSet), .NxtASrc(NPCASrc), .NxtBSrc(NPCBSrc), .Initial_Address(Initial_Address),
    .Imm(idu_1_imm), .BusA(idu_1_busa), .PC(PC));
  BandJ bandj_1 (.Branch(BandJ), .NxtASrc(NPCASrc), .Zero(alu_1_zero), .NxtBSrc(NPCBSrc), .Result0(alu_1_s[0]));
  DataRAM dataram_1 (
    .Addr(alu_1_s[17:0]), .Din(Din), .CLK(clk), .CLR(ReSet), .WE(MemWr), .MemOp(MemOp),
    .DataOut(dataram_1_dataout));  // open: AlignErr
  Multiplexer #(.width(32), .enable("false")) multiplexer_1 (
    .in0(alu_1_s), .in1(dataram_1_dataout), .out(BusW), .sel(MemtoReg));

  // Other names for the same wires on the sheet: Init_Addr[31:0] = Initial_Address

  // Notes on the sheet:
  //   ExtOp: pull=down
  //   ALUBSrc: pull=down
  //   ALUASrc: pull=down
  //   NPCBSrc: pull=down
  //   BandJ: pull=down
  //   ALUctr: pull=down
  //   RegWr: pull=down
  //   NPCASrc: pull=down
  //   contents of rom_1 (hex, n*v repeats v):
  //   8000ef ffdff06f 100013 deadc2b7 eef28293 52d333 135313 4052d3b3 529e33 1e1e13 6e0eb3 1000513 5500a3
  //   551223 551323 552423 150483 154903 451983 655a03 452a83 a55b03 ffff0bb7 17afc33 16c6cb3 fb9e92e3 73
  //   输入信号
  //   请勿修改引脚名称、电路名称及电路封装外观
  //   为了后续实验中的引用，不要修改控制信号的编码定义、引脚名称和在布局中的位置。
  //   指令存储器和数据存储器数据位都是32位，指令存储器编址以字为单位，数据存储器编址以字节为单位。
  //   32位数据存储器，按字节分4片存储，可按照字节、半字和字进行存储；读取字节或半字时，支持0扩展和符号位扩展。
  //   输出信号
endmodule

module BandJ (
  input  [2:0] Branch,
  input  Zero,
  input  Result0,
  output NxtASrc,
  output NxtBSrc
);

  wire not_1_out, or_1_out;

  or or_1 (or_1_out, Zero, ~Result0);  // OR_Gate
  and and_1 (NxtASrc, ~Branch[0], Branch[1], ~Branch[2]);  // AND_Gate
  Multiplexer #(.select(3), .enable("false")) multiplexer_1 (
    .in0(1'b0), .in1(1'b1), .in2(1'b1), .in4(Zero), .in5(not_1_out), .in6(Result0), .in7(or_1_out),
    .out(NxtBSrc), .sel(Branch));  // open: in3
  not not_1 (not_1_out, Zero);

  // Notes on the sheet:
  //   Branch: pull=down
  //   Zero: pull=down
  //   输入信号
  //   请勿修改引脚名称、电路名称及电路封装外观
  //   不要修改控制信号的编码定义、引脚名称和在布局中的位置。
  //   输出信号
endmodule

module IFU (
  input  [31:0] Initial_Address,
  input  [31:0] Imm,
  input  [31:0] BusA,
  input  CLK,
  input  Reset,
  input  NxtASrc,
  input  NxtBSrc,
  output [31:0] PC
);

  wire [31:0] adder_1_out, multiplexer_1_out, multiplexer_2_out, multiplexer_3_out;

  Multiplexer #(.width(32), .enable("false")) multiplexer_1 (
    .in0(adder_1_out), .in1(Initial_Address), .out(multiplexer_1_out), .sel(Reset));
  Register #(.width(32), .Select("high")) \PC寄存器  (.D(multiplexer_1_out), .Q(PC), .clk(CLK));  // open: en, clr
  Multiplexer #(.width(32), .enable("false")) multiplexer_2 (
    .in0(PC), .in1(BusA), .out(multiplexer_2_out), .sel(NxtASrc));
  Multiplexer #(.width(32), .enable("false")) multiplexer_3 (
    .in0(32'h4), .in1(Imm), .out(multiplexer_3_out), .sel(NxtBSrc));
  Adder #(.width(32)) adder_1 (
    .a(multiplexer_2_out), .b(multiplexer_3_out), .out(adder_1_out), .cin(1'b0));  // open: cout

  // Other names for the same wires on the sheet: Init_Addr[31:0] = Initial_Address

  // Notes on the sheet:
  //   Imm: pull=down
  //   NxtBSrc: pull=down
  //   NxtASrc: pull=down
  //   BusA: pull=down
  //   输入信号
  //   请勿修改引脚名称、电路名称及电路封装外观
  //   指令存储器256KB，数据位为32位，地址位为16位。PC寄存器数据宽度32位，片选信号高电平有效
  //   输出信号
endmodule

module IDU (
  input  [31:0] IR,
  input  [31:0] BusW,
  input  [31:0] PC,
  input  [2:0] ExtOp,
  input  RegWr,
  input  ALUASrc,
  input  [1:0] ALUBSrc,
  input  CLK,
  output [31:0] DataA,
  output [31:0] DataB,
  output [31:0] BusA,
  output [31:0] BusB,
  output [6:0] OpCode,
  output [31:0] Imm,
  output [2:0] Funct3,
  output [6:0] Funct7
);

  \立即数扩展器  \u_立即数扩展器_1  (.Instr(IR), .Extop(ExtOp), .imm(Imm));
  RegFile regfile_1 (
    .R1_num(IR[19:15]), .R2_num(IR[24:20]), .Write_Reg_num(IR[11:7]), .Write_Enable(RegWr), .Clock(CLK),
    .Din(BusW), .Reg1Out(BusA), .Reg2Out(BusB));
  Multiplexer #(.width(32), .enable("false")) multiplexer_1 (.in0(BusA), .in1(PC), .out(DataA), .sel(ALUASrc));
  Multiplexer #(.select(2), .width(32), .enable("false")) multiplexer_2 (
    .in0(BusB), .in1(32'h4), .in2(Imm), .out(DataB), .sel(ALUBSrc));  // open: in3

  assign Funct3 = IR[14:12];
  assign Funct7 = IR[31:25];
  assign OpCode = IR[6:0];

  // Other names for the same wires on the sheet: op[6:0] = IR[6:0]

  // Notes on the sheet:
  //   RegWr: pull=down
  //   ALUASrc: pull=down
  //   PC: pull=down
  //   ExtOp: pull=down
  //   BusW: pull=down
  //   ALUBSrc: pull=down
  //   输入信号
  //   为了后续实验中的引用，不要修改ALUASrc、ALUBSrc和EXtOP编码定义。
  //   请勿修改引脚名称、电路名称及电路封装外观
  //   输出信号
  //   修改寄存器堆电路设计，0号寄存器始终为0。
endmodule

module RegFile (
  input  [4:0] R1_num,
  input  [4:0] R2_num,
  input  [4:0] Write_Reg_num,
  input  [31:0] Din,
  input  Write_Enable,
  input  Clock,
  output [31:0] Reg1Out,
  output [31:0] Reg2Out
);

  wire and_1_out, and_2_out, and_3_out, and_4_out, and_5_out, and_6_out, and_7_out, and_8_out, and_9_out,
       and_10_out, and_11_out, and_12_out, and_13_out, and_14_out, and_15_out, and_16_out, and_17_out,
       and_18_out, and_19_out, and_20_out, and_21_out, and_22_out, and_23_out, and_24_out, and_25_out,
       and_26_out, and_27_out, and_28_out, and_29_out, and_30_out, and_31_out, and_32_out, decoder_1_out0,
       decoder_1_out1, decoder_1_out2, decoder_1_out3, decoder_1_out4, decoder_1_out5, decoder_1_out6,
       decoder_1_out7, decoder_1_out8, decoder_1_out9, decoder_1_out10, decoder_1_out11, decoder_1_out12,
       decoder_1_out13, decoder_1_out14, decoder_1_out15, decoder_1_out16, decoder_1_out17, decoder_1_out18,
       decoder_1_out19, decoder_1_out20, decoder_1_out21, decoder_1_out22, decoder_1_out23, decoder_1_out24,
       decoder_1_out25, decoder_1_out26, decoder_1_out27, decoder_1_out28, decoder_1_out29, decoder_1_out30,
       decoder_1_out31;
  wire [31:0] _0_q, _1_q, _2_q, _3_q, _6_q, _7_q, _8_q, _9_q, _15_q, _18_q, _21_q, _24_q, register_1_q,
       register_2_q, register_3_q, register_4_q, register_5_q, register_6_q, register_7_q, register_8_q,
       register_9_q, register_10_q, register_11_q, register_12_q, register_13_q, register_14_q,
       register_15_q, register_16_q, register_17_q, register_18_q, register_19_q, register_20_q;

  Decoder #(.select(5), .enable("false")) decoder_1 (
    .out0(decoder_1_out0), .out1(decoder_1_out1), .out2(decoder_1_out2), .out3(decoder_1_out3),
    .out4(decoder_1_out4), .out5(decoder_1_out5), .out6(decoder_1_out6), .out7(decoder_1_out7),
    .out8(decoder_1_out8), .out9(decoder_1_out9), .out10(decoder_1_out10), .out11(decoder_1_out11),
    .out12(decoder_1_out12), .out13(decoder_1_out13), .out14(decoder_1_out14), .out15(decoder_1_out15),
    .out16(decoder_1_out16), .out17(decoder_1_out17), .out18(decoder_1_out18), .out19(decoder_1_out19),
    .out20(decoder_1_out20), .out21(decoder_1_out21), .out22(decoder_1_out22), .out23(decoder_1_out23),
    .out24(decoder_1_out24), .out25(decoder_1_out25), .out26(decoder_1_out26), .out27(decoder_1_out27),
    .out28(decoder_1_out28), .out29(decoder_1_out29), .out30(decoder_1_out30), .out31(decoder_1_out31),
    .sel(Write_Reg_num));
  and and_1 (and_1_out, Write_Enable, decoder_1_out0);
  and and_2 (and_2_out, Write_Enable, decoder_1_out1);
  and and_3 (and_3_out, Write_Enable, decoder_1_out2);
  and and_4 (and_4_out, Write_Enable, decoder_1_out3);
  and and_5 (and_5_out, Write_Enable, decoder_1_out4);
  and and_6 (and_6_out, Write_Enable, decoder_1_out5);
  and and_7 (and_7_out, Write_Enable, decoder_1_out6);
  and and_8 (and_8_out, Write_Enable, decoder_1_out7);
  and and_9 (and_9_out, Write_Enable, decoder_1_out8);
  and and_10 (and_10_out, Write_Enable, decoder_1_out9);
  and and_11 (and_11_out, Write_Enable, decoder_1_out10);
  and and_12 (and_12_out, Write_Enable, decoder_1_out11);
  and and_13 (and_13_out, Write_Enable, decoder_1_out12);
  and and_14 (and_14_out, Write_Enable, decoder_1_out13);
  and and_15 (and_15_out, Write_Enable, decoder_1_out14);
  and and_16 (and_16_out, Write_Enable, decoder_1_out15);
  and and_17 (and_17_out, Write_Enable, decoder_1_out16);
  and and_18 (and_18_out, Write_Enable, decoder_1_out17);
  and and_19 (and_19_out, Write_Enable, decoder_1_out18);
  and and_20 (and_20_out, Write_Enable, decoder_1_out19);
  and and_21 (and_21_out, Write_Enable, decoder_1_out20);
  and and_22 (and_22_out, Write_Enable, decoder_1_out21);
  and and_23 (and_23_out, Write_Enable, decoder_1_out22);
  and and_24 (and_24_out, Write_Enable, decoder_1_out23);
  and and_25 (and_25_out, Write_Enable, decoder_1_out24);
  and and_26 (and_26_out, Write_Enable, decoder_1_out25);
  and and_27 (and_27_out, Write_Enable, decoder_1_out26);
  and and_28 (and_28_out, Write_Enable, decoder_1_out27);
  and and_29 (and_29_out, Write_Enable, decoder_1_out28);
  and and_30 (and_30_out, Write_Enable, decoder_1_out29);
  and and_31 (and_31_out, Write_Enable, decoder_1_out30);
  and and_32 (and_32_out, Write_Enable, decoder_1_out31);
  Register #(.width(32), .Select("low")) _0 (.D(Din), .en(and_1_out), .Q(_0_q), .clk(Clock), .clr(1'b1));
  Register #(.width(32), .Select("low")) _1 (.D(Din), .en(and_2_out), .Q(_1_q), .clk(Clock));  // open: clr
  Register #(.width(32), .Select("low")) _2 (.D(Din), .en(and_3_out), .Q(_2_q), .clk(Clock));  // open: clr
  Register #(.width(32), .Select("low")) _3 (.D(Din), .en(and_4_out), .Q(_3_q), .clk(Clock));  // open: clr
  Register #(.width(32), .Select("low")) register_1 (
    .D(Din), .en(and_5_out), .Q(register_1_q), .clk(Clock));  // open: clr
  Register #(.width(32), .Select("low")) register_2 (
    .D(Din), .en(and_6_out), .Q(register_2_q), .clk(Clock));  // open: clr
  Register #(.width(32), .Select("low")) _6 (.D(Din), .en(and_7_out), .Q(_6_q), .clk(Clock));  // open: clr
  Register #(.width(32), .Select("low")) _7 (.D(Din), .en(and_8_out), .Q(_7_q), .clk(Clock));  // open: clr
  Register #(.width(32), .Select("low")) _8 (.D(Din), .en(and_9_out), .Q(_8_q), .clk(Clock));  // open: clr
  Register #(.width(32), .Select("low")) _9 (.D(Din), .en(and_10_out), .Q(_9_q), .clk(Clock));  // open: clr
  Register #(.width(32), .Select("low")) register_3 (
    .D(Din), .en(and_11_out), .Q(register_3_q), .clk(Clock));  // open: clr
  Register #(.width(32), .Select("low")) register_4 (
    .D(Din), .en(and_12_out), .Q(register_4_q), .clk(Clock));  // open: clr
  Register #(.width(32), .Select("low")) register_5 (
    .D(Din), .en(and_13_out), .Q(register_5_q), .clk(Clock));  // open: clr
  Register #(.width(32), .Select("low")) register_6 (
    .D(Din), .en(and_14_out), .Q(register_6_q), .clk(Clock));  // open: clr
  Register #(.width(32), .Select("low")) register_7 (
    .D(Din), .en(and_15_out), .Q(register_7_q), .clk(Clock));  // open: clr
  Register #(.width(32), .Select("low")) _15 (.D(Din), .en(and_16_out), .Q(_15_q), .clk(Clock));  // open: clr
  Register #(.width(32), .Select("low")) register_8 (
    .D(Din), .en(and_17_out), .Q(register_8_q), .clk(Clock));  // open: clr
  Register #(.width(32), .Select("low")) register_9 (
    .D(Din), .en(and_18_out), .Q(register_9_q), .clk(Clock));  // open: clr
  Register #(.width(32), .Select("low")) _18 (.D(Din), .en(and_19_out), .Q(_18_q), .clk(Clock));  // open: clr
  Register #(.width(32), .Select("low")) register_10 (
    .D(Din), .en(and_20_out), .Q(register_10_q), .clk(Clock));  // open: clr
  Register #(.width(32), .Select("low")) register_11 (
    .D(Din), .en(and_21_out), .Q(register_11_q), .clk(Clock));  // open: clr
  Register #(.width(32), .Select("low")) _21 (.D(Din), .en(and_22_out), .Q(_21_q), .clk(Clock));  // open: clr
  Register #(.width(32), .Select("low")) register_12 (
    .D(Din), .en(and_23_out), .Q(register_12_q), .clk(Clock));  // open: clr
  Register #(.width(32), .Select("low")) register_13 (
    .D(Din), .en(and_24_out), .Q(register_13_q), .clk(Clock));  // open: clr
  Register #(.width(32), .Select("low")) _24 (.D(Din), .en(and_25_out), .Q(_24_q), .clk(Clock));  // open: clr
  Register #(.width(32), .Select("low")) register_14 (
    .D(Din), .en(and_26_out), .Q(register_14_q), .clk(Clock));  // open: clr
  Register #(.width(32), .Select("low")) register_15 (
    .D(Din), .en(and_27_out), .Q(register_15_q), .clk(Clock));  // open: clr
  Register #(.width(32), .Select("low")) register_16 (
    .D(Din), .en(and_28_out), .Q(register_16_q), .clk(Clock));  // open: clr
  Register #(.width(32), .Select("low")) register_17 (
    .D(Din), .en(and_29_out), .Q(register_17_q), .clk(Clock));  // open: clr
  Register #(.width(32), .Select("low")) register_18 (
    .D(Din), .en(and_30_out), .Q(register_18_q), .clk(Clock));  // open: clr
  Register #(.width(32), .Select("low")) register_19 (
    .D(Din), .en(and_31_out), .Q(register_19_q), .clk(Clock));  // open: clr
  Register #(.width(32), .Select("low")) register_20 (
    .D(Din), .en(and_32_out), .Q(register_20_q), .clk(Clock));  // open: clr
  Multiplexer #(.select(5), .width(32), .enable("false")) multiplexer_1 (
    .in0(_0_q), .in1(_1_q), .in2(_2_q), .in3(_3_q), .in4(register_1_q), .in5(register_2_q), .in6(_6_q),
    .in7(_7_q), .in8(_8_q), .in9(_9_q), .in10(register_3_q), .in11(register_4_q), .in12(register_5_q),
    .in13(register_6_q), .in14(register_7_q), .in15(_15_q), .in16(register_8_q), .in17(register_9_q),
    .in18(_18_q), .in19(register_10_q), .in20(register_11_q), .in21(_21_q), .in22(register_12_q),
    .in23(register_13_q), .in24(_24_q), .in25(register_14_q), .in26(register_15_q), .in27(register_16_q),
    .in28(register_17_q), .in29(register_18_q), .in30(register_19_q), .in31(register_20_q), .out(Reg1Out),
    .sel(R1_num));
  Multiplexer #(.select(5), .width(32), .enable("false")) multiplexer_2 (
    .in0(_0_q), .in1(_1_q), .in2(_2_q), .in3(_3_q), .in4(register_1_q), .in5(register_2_q), .in6(_6_q),
    .in7(_7_q), .in8(_8_q), .in9(_9_q), .in10(register_3_q), .in11(register_4_q), .in12(register_5_q),
    .in13(register_6_q), .in14(register_7_q), .in15(_15_q), .in16(register_8_q), .in17(register_9_q),
    .in18(_18_q), .in19(register_10_q), .in20(register_11_q), .in21(_21_q), .in22(register_12_q),
    .in23(register_13_q), .in24(_24_q), .in25(register_14_q), .in26(register_15_q), .in27(register_16_q),
    .in28(register_17_q), .in29(register_18_q), .in30(register_19_q), .in31(register_20_q), .out(Reg2Out),
    .sel(R2_num));

  // Other names for the same wires on the sheet: CLK = Clock; RA[4:0] = R1_num; RB[4:0] = R2_num; RDA[31:0] = Reg1Out;
  //   RDB[31:0] = Reg2Out; RW[4:0] = Write_Reg_num; WE = Write_Enable

  // Notes on the sheet:
  //   输入引脚
  //   请勿修改引脚名称、电路名称及电路封装外观
  //   提示：使用译码器、多路选择器和32位寄存器及逻辑门实现寄存器堆，禁止直接使用存储器组件。
  //   输出引脚
endmodule

module \立即数扩展器  (
  input  [31:0] Instr,
  input  [2:0] Extop,
  output [31:0] imm
);

  wire [11:0] bit_extender_1_out;
  wire [19:0] bit_extender_2_out;

  assign bit_extender_1_out = {{11{Instr[31]}}, Instr[31]};  // Bit_Extender bit_extender_1
  assign bit_extender_2_out = {{19{Instr[31]}}, Instr[31]};  // Bit_Extender bit_extender_2
  Multiplexer #(.select(3), .width(32), .enable("false")) multiplexer_1 (
    .in0({bit_extender_2_out, Instr[31:20]}), .in1({Instr[31:12], {12{1'b0}}}),
    .in2({bit_extender_2_out, Instr[31:25], Instr[11:7]}),
    .in3({bit_extender_2_out, Instr[7], Instr[30:25], Instr[11:8], 1'b0}),
    .in4({bit_extender_1_out, Instr[19:12], Instr[20], Instr[30:21], 1'b0}), .out(imm), .sel(Extop));  // open: in5, in6, in7

  // Notes on the sheet:
  //   Instr: pull=down
  //   Extop: pull=down
  //   输入引脚
  //   输出引脚
endmodule

module DataRAM (
  input  CLK,
  input  CLR,
  input  WE,
  input  [2:0] MemOp,
  input  [17:0] Addr,
  input  [31:0] Din,
  output AlignErr,
  output [31:0] DataOut
);

  wire \_1位 , \_2位 , \_4位 , and_1_out, and_2_out, and_3_out, and_4_out, and_5_out, and_6_out, and_7_out,
       and_8_out, and_9_out, and_10_out, and_13_out, and_14_out, nor_1_out, or_1_out, SEL0, SEL1, SEL2, SEL3,
       \写入 ;
  wire [7:0] multiplexer_1_out, multiplexer_2_out, multiplexer_3_out, multiplexer_4_out;
  wire [15:0] multiplexer_5_out;
  wire [31:0] bit_extender_1_out, bit_extender_2_out, bit_extender_3_out, bit_extender_4_out, \低8位_data ;

  Multiplexer #(.width(8), .enable("false")) multiplexer_1 (
    .in0(Din[7:0]), .in1(Din[15:8]), .out(multiplexer_1_out), .sel(SEL0));
  Multiplexer #(.width(8), .enable("false")) multiplexer_2 (
    .in0(Din[7:0]), .in1(Din[23:16]), .out(multiplexer_2_out), .sel(SEL0));
  Multiplexer #(.select(2), .width(8), .enable("false")) multiplexer_3 (
    .in0(Din[7:0]), .in2(Din[15:8]), .in3(Din[31:24]), .out(multiplexer_3_out), .sel({SEL2, SEL0}));  // open: in1
  and and_1 (and_1_out, WE, \写入 );
  nor nor_1 (nor_1_out, \_1位 , \_4位 , \_2位 );
  and and_2 (and_2_out, \_4位 , ~Addr[0], ~Addr[1]);  // AND_Gate
  and and_3 (and_3_out, \_1位 , Addr[0], Addr[1]);
  and and_4 (and_4_out, \_2位 , ~Addr[0], Addr[1]);  // AND_Gate
  and and_5 (and_5_out, \_1位 , ~Addr[0], Addr[1]);  // AND_Gate
  and and_6 (and_6_out, \_1位 , Addr[0], ~Addr[1]);  // AND_Gate
  and and_7 (and_7_out, \_2位 , ~Addr[0], ~Addr[1]);  // AND_Gate
  and and_8 (and_8_out, \_1位 , ~Addr[0], ~Addr[1]);  // AND_Gate
  and and_9 (and_9_out, \_2位 , Addr[0]);
  and and_10 (and_10_out, \_4位 , or_1_out);
  or or_1 (or_1_out, Addr[0], Addr[1]);
  and and_11 (\_1位 , MemOp[0], ~MemOp[1]);  // AND_Gate
  and and_12 (\_2位 , ~MemOp[0], MemOp[1]);  // AND_Gate
  nor nor_2 (\_4位 , MemOp[0], MemOp[1], MemOp[2]);
  and and_13 (and_13_out, MemOp[0], ~MemOp[1], MemOp[2]);  // AND_Gate
  and and_14 (and_14_out, ~MemOp[0], MemOp[1], MemOp[2]);  // AND_Gate
  or or_2 (SEL3, and_2_out, and_3_out, and_4_out);
  or or_3 (SEL2, and_2_out, and_5_out, and_4_out);
  or or_4 (SEL1, and_2_out, and_6_out, and_7_out);
  or or_5 (SEL0, and_2_out, and_8_out, and_7_out);
  or or_6 (AlignErr, and_9_out, nor_1_out, and_10_out);
  or or_7 (\写入 , \_4位 , and_13_out, and_14_out);
  RAM #(.addrWidth(16), .bus("separate"), .Select("high"), .simpleMode("false")) \u_低8位  (
    .addr(Addr[17:2]), .din(Din[7:0]), .data(\低8位_data [7:0]), .str(and_1_out), .sel(SEL0), .clk(CLK),
    .clr(CLR));  // open: ld
  RAM #(.addrWidth(16), .bus("separate"), .Select("high"), .simpleMode("false")) ram_1 (
    .addr(Addr[17:2]), .din(multiplexer_1_out), .data(\低8位_data [15:8]), .str(and_1_out), .sel(SEL1),
    .clk(CLK), .clr(CLR));  // open: ld
  RAM #(.addrWidth(16), .bus("separate"), .Select("high"), .simpleMode("false")) ram_2 (
    .addr(Addr[17:2]), .din(multiplexer_2_out), .data(\低8位_data [23:16]), .str(and_1_out), .sel(SEL2),
    .clk(CLK), .clr(CLR));  // open: ld
  RAM #(.addrWidth(16), .bus("separate"), .Select("high"), .simpleMode("false")) \u_高8位  (
    .addr(Addr[17:2]), .din(multiplexer_3_out), .data(\低8位_data [31:24]), .str(and_1_out), .sel(SEL3),
    .clk(CLK), .clr(CLR));  // open: ld
  Multiplexer #(.select(2), .width(8), .enable("false")) multiplexer_4 (
    .in0(\低8位_data [7:0]), .in1(\低8位_data [15:8]), .in2(\低8位_data [23:16]), .in3(\低8位_data [31:24]),
    .out(multiplexer_4_out), .sel(Addr[1:0]));
  Multiplexer #(.select(2), .width(16), .enable("false")) multiplexer_5 (
    .in0(\低8位_data [15:0]), .in2(\低8位_data [31:16]), .out(multiplexer_5_out), .sel(Addr[1:0]));  // open: in1, in3
  assign bit_extender_1_out = {{24{1'b0}}, multiplexer_4_out};  // Bit_Extender bit_extender_1
  assign bit_extender_2_out = {{16{1'b0}}, multiplexer_5_out};  // Bit_Extender bit_extender_2
  assign bit_extender_3_out = {{24{multiplexer_4_out[7]}}, multiplexer_4_out};  // Bit_Extender bit_extender_3
  assign bit_extender_4_out = {{16{multiplexer_5_out[15]}}, multiplexer_5_out};  // Bit_Extender bit_extender_4
  Multiplexer #(.select(3), .width(32), .enable("false")) multiplexer_6 (
    .in0(\低8位_data ), .in1(bit_extender_1_out), .in2(bit_extender_2_out), .in5(bit_extender_3_out),
    .in6(bit_extender_4_out), .out(DataOut), .sel(MemOp));  // open: in3, in4, in7

  // Other names for the same wires on the sheet: addr2[1:0] = Addr[1:0]; Dout[31:0] = DataOut

  // Notes on the sheet:
  //   输入引脚
  //   请勿修改引脚名称、电路名称及电路封装外观
  //   为了后续实验中的引用，不要修改MemOp的编码定义、引脚名称和在布局中的位置。
  //   32位数据存储器，按字节分4片存储，可按照字节、半字和字进行存储；读取字节或半字时，支持0扩展和符号位扩展。
  //   输出引脚
endmodule

module ALU (
  input  [3:0] ALUctr,
  input  [31:0] A,
  input  [31:0] B,
  output Zero,
  output [31:0] S
);

  wire adder32_1_cf, adder32_1_of, adder32_1_sf, aluctrl_1_alctr, aluctrl_1_sftctr, aluctrl_1_sigctr,
       aluctrl_1_subctr, multiplexer_2_out, xor_4_out;
  wire [2:0] aluctrl_1_opctr;
  wire [31:0] adder32_1_s, and_1_out, bit_extender_1_out, bit_extender_2_out, or_1_out, shifter32_1_dataout,
       xor_1_out, xor_2_out, xor_3_out;

  assign bit_extender_1_out = {{31{aluctrl_1_subctr}}, aluctrl_1_subctr};  // Bit_Extender bit_extender_1
  assign xor_1_out = B ^ bit_extender_1_out;  // XOR_Gate xor_1, 32 bits wide
  assign and_1_out = A & B;  // AND_Gate and_1, 32 bits wide
  assign or_1_out = A | B;  // OR_Gate or_1, 32 bits wide
  assign xor_2_out = A ^ B;  // XOR_Gate xor_2, 32 bits wide
  Shifter32 shifter32_1 (
    .DataIn(A), .shamt(B[4:0]), .L_R(aluctrl_1_sftctr), .A_L(aluctrl_1_alctr), .DataOut(shifter32_1_dataout));
  Adder32 adder32_1 (
    .CF(adder32_1_cf), .OF(adder32_1_of), .SF(adder32_1_sf), .ZF(Zero), .X(A), .Y(xor_1_out),
    .Cin(aluctrl_1_subctr), .S(adder32_1_s));  // open: Cout
  assign xor_3_out = and_1_out ^ or_1_out;  // XOR_Gate xor_3, 32 bits wide
  xor xor_4 (xor_4_out, adder32_1_of, adder32_1_sf);
  Multiplexer #(.select(3), .width(32), .enable("false")) multiplexer_1 (
    .in0(adder32_1_s), .in1(and_1_out), .in2(or_1_out), .in3(xor_2_out), .in4(shifter32_1_dataout), .in5(B),
    .in6(bit_extender_2_out), .in7(xor_3_out), .out(S), .sel(aluctrl_1_opctr));
  ALUctrl aluctrl_1 (
    .SUBctr(aluctrl_1_subctr), .SFTctr(aluctrl_1_sftctr), .SIGctr(aluctrl_1_sigctr), .ALctr(aluctrl_1_alctr),
    .OPctr(aluctrl_1_opctr), .ALUctr(ALUctr));
  // Probe on A
  // Probe on B
  // Probe on S
  Multiplexer #(.enable("false")) multiplexer_2 (
    .in0(adder32_1_cf), .in1(xor_4_out), .out(multiplexer_2_out), .sel(aluctrl_1_sigctr));
  assign bit_extender_2_out = {{31{1'b0}}, multiplexer_2_out};  // Bit_Extender bit_extender_2

  // Other names for the same wires on the sheet: Result[31:0] = S

  // Notes on the sheet:
  //   B: pull=down
  //   A: pull=down
  //   ALUctr: pull=down
  //   输入引脚
  //   请勿修改引脚名称、电路名称及电路封装外观
  //   提示：使用32位并行加法器子电路、桶形移位器、ALU控制子电路实现32位ALU
  //   功能说明:32位ALU，输入32位操作数A、B，4位控制信号ALUctr，输出32位结果Reseult和1位Zero标志位
  //   输出引脚
  //   操作数和结果
endmodule

module ALUctrl (
  input  [3:0] ALUctr,
  output SUBctr,
  output SFTctr,
  output SIGctr,
  output ALctr,
  output [2:0] OPctr
);

  wire and_3_out, and_4_out, and_5_out, and_6_out, and_7_out, and_8_out, and_9_out, and_11_out, or_2_out,
       or_3_out, or_4_out;

  and and_1 (SFTctr, ALUctr[0], ~ALUctr[1], ~ALUctr[2], ~ALUctr[3]);  // AND_Gate
  and and_2 (SIGctr, ~ALUctr[0], ALUctr[1], ~ALUctr[2], ~ALUctr[3]);  // AND_Gate
  and and_3 (and_3_out, ALUctr[1], ALUctr[1], ~ALUctr[2], ~ALUctr[3]);  // AND_Gate
  and and_4 (and_4_out, ~ALUctr[0], ~ALUctr[1], ALUctr[2], ~ALUctr[3]);  // AND_Gate
  and and_5 (and_5_out, ALUctr[0], ~ALUctr[1], ALUctr[2], ~ALUctr[3]);  // AND_Gate
  and and_6 (and_6_out, ~ALUctr[0], ALUctr[1], ALUctr[2], ~ALUctr[3]);  // AND_Gate
  and and_7 (and_7_out, ALUctr[0], ALUctr[1], ALUctr[2], ~ALUctr[3]);  // AND_Gate
  and and_8 (and_8_out, ~ALUctr[1], ~ALUctr[1], ~ALUctr[2], ALUctr[3]);  // AND_Gate
  and and_9 (and_9_out, ~ALUctr[0], ~ALUctr[1], ALUctr[2], ALUctr[3]);  // AND_Gate
  and and_10 (ALctr, ALUctr[0], ~ALUctr[1], ALUctr[2], ALUctr[3]);  // AND_Gate
  and and_11 (and_11_out, ALUctr[0], ALUctr[1], ALUctr[2], ALUctr[3]);
  or or_1 (SUBctr, SIGctr, and_3_out, and_8_out);
  or or_2 (or_2_out, SIGctr, and_3_out, and_4_out, and_6_out);
  or or_3 (or_3_out, and_4_out, and_7_out, and_11_out);
  or or_4 (or_4_out, SFTctr, SIGctr, and_3_out, and_5_out, ALctr, and_11_out);
  or or_5 (OPctr[1], or_2_out, and_9_out);
  or or_6 (OPctr[0], or_3_out, and_9_out);
  or or_7 (OPctr[2], or_4_out, and_9_out);

  // Other names for the same wires on the sheet: LRctr = SFTctr

  // Notes on the sheet:
  //   输入引脚
  //   ALU操作控制信号生成部件
  //   m13
  //   输出引脚
endmodule

module Adder32 (
  input  Cin,
  input  [31:0] X,
  input  [31:0] Y,
  output CF,
  output Cout,
  output OF,
  output SF,
  output [31:0] S,
  output ZF
);

  wire adder16_1_c16, and_1_out, and_2_out, not_1_out, not_2_out, not_3_out, or_1_out, or_2_out;

  Adder16 adder16_1 (.X(X[15:0]), .Y(Y[15:0]), .C0(Cin), .S(S[15:0]), .C16(adder16_1_c16));  // open: Pg, Gg
  Adder16 adder16_2 (.X(X[31:16]), .Y(Y[31:16]), .C0(adder16_1_c16), .S(S[31:16]), .C16(Cout));  // open: Pg, Gg
  xor xor_1 (CF, Cout, Cin);
  not not_1 (not_1_out, Y[31]);
  not not_2 (not_2_out, X[31]);
  not not_3 (not_3_out, S[31]);
  // Probe on X
  // Probe on Y
  // Probe on S
  or or_1 (or_1_out, S[0], S[1], S[2], S[3], S[4], S[5], S[6], S[7], S[8], S[9], S[10], S[11], S[12], S[13], S[14], S[15]);
  or or_2 (or_2_out, S[16], S[17], S[18], S[19], S[20], S[21], S[22], S[23], S[24], S[25], S[26], S[27], S[28], S[29], S[30], S[31]);
  and and_1 (and_1_out, S[31], not_1_out, not_2_out);
  and and_2 (and_2_out, not_3_out, Y[31], X[31]);
  or or_3 (OF, and_1_out, and_2_out);
  nor nor_1 (ZF, or_1_out, or_2_out);

  assign SF = S[31];

  // Other names for the same wires on the sheet: Xn_1 = X[31]; Yn_1 = Y[31]

  // Notes on the sheet:
  //   Cin: pull=down
  //   Y: pull=down
  //   X: pull=down
  //   输入引脚区
  //   输出引脚区
  //   请勿修改引脚名称、电路名称及电路封装外观
  //   提示：使用16位并行加法器子电路实现32位快速加法器
  //   功能说明:32位Adder  S=X+Y，Cout为最高位进位位，Cin为进位输入， S为和，溢出OF、进位CF、零ZF、符号SF。
  //   +
  //   =
  //   无符号加法
endmodule

// 移位器
module Shifter32 (
  input  [4:0] shamt,
  input  L_R,
  input  A_L,
  input  [31:0] DataIn,
  output [31:0] DataOut
);

  wire and_1_out;
  wire [0:0] multiplexer_1_out;
  wire [1:0] multiplexer_3_out;
  wire [3:0] multiplexer_5_out;
  wire [7:0] multiplexer_6_out_2, multiplexer_7_out;
  wire [15:0] multiplexer_8_out, multiplexer_8_out_2, multiplexer_9_out;
  wire [23:0] multiplexer_6_out;
  wire [31:0] bit_extender_1_out, bit_extender_2_out, bit_extender_3_out, bit_extender_4_out,
       bit_extender_5_out, multiplexer_2_out, multiplexer_4_out;

  and and_1 (and_1_out, A_L, DataIn[31]);
  assign bit_extender_1_out = {{1{and_1_out}}, DataIn[31:1]};  // Bit_Extender bit_extender_1
  Multiplexer #(.enable("false")) multiplexer_1 (.in0(1'b0), .in1(DataIn[31]), .out(multiplexer_1_out[0]), .sel(A_L));
  Multiplexer #(.select(2), .width(32), .enable("false")) multiplexer_2 (
    .in0(DataIn), .in1(DataIn), .in2(bit_extender_1_out), .in3({DataIn[30:0], multiplexer_1_out[0]}),
    .out(multiplexer_2_out), .sel({shamt[0], L_R}));
  assign bit_extender_2_out = {{2{and_1_out}}, multiplexer_2_out[31:2]};  // Bit_Extender bit_extender_2
  Multiplexer #(.width(2), .enable("false")) multiplexer_3 (
    .in0(2'b00), .in1(multiplexer_2_out[31:30]), .out(multiplexer_3_out), .sel(A_L));
  Multiplexer #(.select(2), .width(32), .enable("false")) multiplexer_4 (
    .in0(multiplexer_2_out), .in1(multiplexer_2_out), .in2(bit_extender_2_out),
    .in3({multiplexer_2_out[29:0], multiplexer_3_out}), .out(multiplexer_4_out), .sel({shamt[1], L_R}));
  assign bit_extender_3_out = {{4{and_1_out}}, multiplexer_4_out[31:4]};  // Bit_Extender bit_extender_3
  Multiplexer #(.width(4), .enable("false")) multiplexer_5 (
    .in0(4'b0000), .in1(multiplexer_4_out[31:28]), .out(multiplexer_5_out), .sel(A_L));
  Multiplexer #(.select(2), .width(32), .enable("false")) multiplexer_6 (
    .in0(multiplexer_4_out), .in1(multiplexer_4_out), .in2(bit_extender_3_out),
    .in3({multiplexer_4_out[27:0], multiplexer_5_out}), .out({multiplexer_6_out, multiplexer_6_out_2}),
    .sel({shamt[2], L_R}));
  assign bit_extender_4_out = {{8{and_1_out}}, multiplexer_6_out};  // Bit_Extender bit_extender_4
  Multiplexer #(.width(8), .enable("false")) multiplexer_7 (
    .in0({8{1'b0}}), .in1(multiplexer_6_out[23:16]), .out(multiplexer_7_out), .sel(A_L));
  Multiplexer #(.select(2), .width(32), .enable("false")) multiplexer_8 (
    .in0({multiplexer_6_out, multiplexer_6_out_2}), .in1({multiplexer_6_out, multiplexer_6_out_2}),
    .in2(bit_extender_4_out), .in3({multiplexer_6_out[15:0], multiplexer_6_out_2, multiplexer_7_out}),
    .out({multiplexer_8_out, multiplexer_8_out_2}), .sel({shamt[3], L_R}));
  assign bit_extender_5_out = {{16{and_1_out}}, multiplexer_8_out};  // Bit_Extender bit_extender_5
  Multiplexer #(.width(16), .enable("false")) multiplexer_9 (
    .in0({16{1'b0}}), .in1(multiplexer_8_out), .out(multiplexer_9_out), .sel(A_L));
  Multiplexer #(.select(2), .width(32), .enable("false")) multiplexer_10 (
    .in0({multiplexer_8_out, multiplexer_8_out_2}), .in1({multiplexer_8_out, multiplexer_8_out_2}),
    .in2(bit_extender_5_out), .in3({multiplexer_8_out_2, multiplexer_9_out}), .out(DataOut),
    .sel({shamt[4], L_R}));

  // Other names for the same wires on the sheet: Din[31:0] = DataIn; Left_Right = L_R; Arth_Logic = A_L;
  //   Dout[31:0] = DataOut

  // Notes on the sheet:
  //   L/R,A/L: 00逻辑右移，01算术右移，10逻辑左移，11：循环左移
  //   输入引脚
  //   请勿修改引脚名称、电路名称及电路封装外观
  //   提示：使用多路选择器、逻辑门实现32位桶形移位器，禁止直接使用移位器组件。
  //   输出引脚
endmodule

module Adder16 (
  input  C0,
  input  [15:0] X,
  input  [15:0] Y,
  output C16,
  output Pg,
  output Gg,
  output [15:0] S
);

  wire cla4_1_gg, cla4_1_pg, cla4_2_gg, cla4_2_pg, cla4_3_gg, cla4_3_pg, cla4_4_gg, cla4_4_pg, clu4_1_c1,
       clu4_1_c2, clu4_1_c3;

  CLA4 cla4_1 (.X(X[3:0]), .F(S[3:0]), .Y(Y[3:0]), .Pg(cla4_1_pg), .Cin(C0), .Gg(cla4_1_gg));  // open: Cout
  CLA4 cla4_2 (.X(X[7:4]), .F(S[7:4]), .Y(Y[7:4]), .Pg(cla4_2_pg), .Cin(clu4_1_c1), .Gg(cla4_2_gg));  // open: Cout
  CLU4 clu4_1 (
    .P0(cla4_1_pg), .P1(cla4_2_pg), .P2(cla4_3_pg), .P3(cla4_4_pg), .C1(clu4_1_c1), .C3(clu4_1_c3),
    .G0(cla4_1_gg), .G1(cla4_2_gg), .G2(cla4_3_gg), .G3(cla4_4_gg), .C2(clu4_1_c2), .C0(C0), .Pg(Pg), .Gg(Gg));  // open: C4
  CLA4 cla4_3 (.X(X[11:8]), .F(S[11:8]), .Y(Y[11:8]), .Pg(cla4_3_pg), .Cin(clu4_1_c2), .Gg(cla4_3_gg));  // open: Cout
  CLA4 cla4_4 (.X(X[15:12]), .F(S[15:12]), .Cout(C16), .Y(Y[15:12]), .Pg(cla4_4_pg), .Cin(clu4_1_c3), .Gg(cla4_4_gg));
  // Probe on X
  // Probe on Y
  // Probe on S

  // Notes on the sheet:
  //   C0: pull=down
  //   Y: pull=down
  //   X: pull=down
  //   输入引脚区
  //   请勿修改引脚名称、电路名称及电路封装外观
  //   提示：使用4位先行进位加法器和CLU子电路实现16位并行加法器
  //   功能说明:16位Adder  S=X+Y，C16为最高位进位位，C0为进位输入， Pg、Gg为成组进位生成传递函数
  //   输出引脚区
  //   +
  //   =
  //   无符号加法
endmodule

module CLA4 (
  input  [3:0] X,
  input  [3:0] Y,
  input  Cin,
  output [3:0] F,
  output Cout,
  output Pg,
  output Gg
);

  wire clu4_1_c1, clu4_1_c2, clu4_1_c3, fa_1_g, fa_1_p, fa_2_g, fa_2_p, fa_3_g, fa_3_p, fa_4_g, fa_4_p;

  Hex_Digit_Display hex_digit_display_1 (.value(X));  // open: dp
  FA fa_1 (.A(X[3]), .F(F[3]), .B(Y[3]), .P(fa_1_p), .Cin(clu4_1_c3), .G(fa_1_g));
  Hex_Digit_Display hex_digit_display_2 (.value(Y));  // open: dp
  FA fa_2 (.A(X[2]), .F(F[2]), .B(Y[2]), .P(fa_2_p), .Cin(clu4_1_c2), .G(fa_2_g));
  FA fa_3 (.A(X[1]), .F(F[1]), .B(Y[1]), .P(fa_3_p), .Cin(clu4_1_c1), .G(fa_3_g));
  Hex_Digit_Display hex_digit_display_3 (.value(F));  // open: dp
  CLU4 clu4_1 (
    .P0(fa_4_p), .P1(fa_3_p), .P2(fa_2_p), .P3(fa_1_p), .C1(clu4_1_c1), .C3(clu4_1_c3), .G0(fa_4_g),
    .G1(fa_3_g), .G2(fa_2_g), .G3(fa_1_g), .C2(clu4_1_c2), .C4(Cout), .C0(Cin), .Pg(Pg), .Gg(Gg));
  FA fa_4 (.A(X[0]), .F(F[0]), .B(Y[0]), .P(fa_4_p), .Cin(Cin), .G(fa_4_g));

  // Other names for the same wires on the sheet: Z[3:0] = F

  // Notes on the sheet:
  //   +
  //   =
  //   输出
  //   输入
  //   请勿修改引脚名称、电路名称及电路封装外观
  //   提示：使用全加器和CLU子电路实现四位先行进位加法器CLA4
endmodule

module CLU4 (
  input  P0,
  input  P1,
  input  P2,
  input  P3,
  input  G0,
  input  G1,
  input  G2,
  input  G3,
  input  C0,
  output C1,
  output C3,
  output C2,
  output C4,
  output Pg,
  output Gg
);

  wire and_1_out, and_2_out, and_3_out, and_4_out, and_5_out, and_6_out, and_8_out, and_9_out, and_10_out,
       and_11_out;

  and and_1 (and_1_out, C0, P0);
  and and_2 (and_2_out, P1, C0, P0);
  and and_3 (and_3_out, P1, G0);
  and and_4 (and_4_out, C0, P0, P1, P2);
  and and_5 (and_5_out, G0, P2, P1);
  and and_6 (and_6_out, G1, P2);
  and and_7 (Pg, P0, P1, P2, P3);
  and and_8 (and_8_out, G0, P1, P2, P3);
  and and_9 (and_9_out, G1, P2, P3);
  and and_10 (and_10_out, G2, P3);
  or or_1 (C1, and_1_out, G0);
  or or_2 (C2, and_2_out, and_3_out, G1);
  or or_3 (C3, and_4_out, and_5_out, and_6_out, G2);
  and and_11 (and_11_out, C0, Pg);
  or or_4 (Gg, and_8_out, and_9_out, and_10_out, G3);
  or or_5 (C4, and_11_out, Gg);

  // Notes on the sheet:
  //   输入引脚
  //   请勿修改引脚名称、电路名称及电路封装外观
  //   提示：使用逻辑门电路实现4位四位先行进位部件CLU，Pg、Gg为成组进位生成传递函数
  //   输出引脚
endmodule

module FA (
  input  A,
  input  B,
  input  Cin,
  output F,
  output P,
  output G
);

  xor xor_1 (F, A, B, Cin);
  and and_1 (G, A, B);
  or or_1 (P, A, B);

  // Notes on the sheet:
  //   输入引脚
  //   请勿修改引脚名称、电路名称及电路封装外观
  //   输出引脚
endmodule
