// Logisim project lab6.1.circ as structural Verilog: 1 circuit, main circuit 控制器
module \控制器  (
  input  [6:0] opcode,
  input  [2:0] funct3,
  input  [6:0] funct7,
  output [2:0] ExtOp,
  output RegWr,
  output [2:0] BandJ,
  output ALUASrc,
  output [1:0] ALUBSrc,
  output [3:0] ALUctr,
  output MemtoReg,
  output [2:0] MemOp,
  output MemWr
);

  wire and_1_out, and_2_out, and_3_out, and_5_out, and_6_out, and_7_out, and_9_out, auipc, Halt, I_ALU_out,
       jalr, lui_out, multiplexer_2_out, or_1_out, or_4_out, or_14_out, R_out, srli, \禁用func7 , \禁用func7_2 ;
  wire [2:0] multiplexer_1_out;

  and R (R_out, ~opcode[6], opcode[5], opcode[4], ~opcode[3], ~opcode[2], opcode[1], opcode[0]);  // AND_Gate
  or or_1 (or_1_out, R_out, I_ALU_out);
  and I_ALU (I_ALU_out, ~opcode[6], ~opcode[5], opcode[4], ~opcode[3], ~opcode[2], opcode[1], opcode[0]);  // AND_Gate
  and lui (lui_out, ~opcode[6], opcode[5], opcode[4], ~opcode[3], opcode[2], opcode[1], opcode[0]);  // AND_Gate
  and and_1 (and_1_out, or_1_out, funct3[2]);
  and and_2 (and_2_out, or_1_out, funct3[1]);
  and and_3 (and_3_out, or_1_out, funct3[0]);
  and and_4 (srli, I_ALU_out, and_5_out);
  and and_5 (and_5_out, funct3[0], ~funct3[1], funct3[2]);  // AND_Gate
  and load (MemtoReg, ~opcode[6], ~opcode[5], ~opcode[4], ~opcode[3], ~opcode[2], opcode[1], opcode[0]);  // AND_Gate
  and store (MemWr, ~opcode[6], opcode[5], ~opcode[4], ~opcode[3], ~opcode[2], opcode[1], opcode[0]);  // AND_Gate
  and B (BandJ[2], opcode[6], opcode[5], ~opcode[4], ~opcode[3], ~opcode[2], opcode[1], opcode[0]);  // AND_Gate
  and and_6 (and_6_out, BandJ[2], funct3[1], funct3[2]);
  and Jal (ExtOp[2], opcode[6], opcode[5], ~opcode[4], opcode[3], opcode[2], opcode[1], opcode[0]);  // AND_Gate
  or or_2 (ExtOp[1], BandJ[2], MemWr);
  and and_7 (and_7_out, funct3[2], BandJ[2]);
  and and_8 (auipc, ~opcode[6], ~opcode[5], opcode[4], ~opcode[3], opcode[2], opcode[1], opcode[0]);  // AND_Gate
  or or_3 (RegWr, auipc, R_out, I_ALU_out, lui_out, MemtoReg, ExtOp[2], jalr);
  buf or_4 (or_4_out, lui_out);  // OR_Gate
  or or_5 (ALUctr[2], lui_out, and_1_out);
  or or_6 (ALUctr[1], lui_out, BandJ[2], and_2_out);
  or or_7 (ALUctr[0], lui_out, and_6_out, and_3_out);
  or or_8 (ALUASrc, ExtOp[2], jalr, auipc);
  or or_9 (ExtOp[0], auipc, lui_out, BandJ[2]);
  and and_9 (and_9_out, BandJ[2], funct3[0]);
  or or_10 (BandJ[0], and_9_out, ExtOp[2]);
  or or_11 (BandJ[1], and_7_out, jalr);
  or or_12 (ALUBSrc[0], jalr, ExtOp[2]);
  or or_13 (ALUBSrc[1], I_ALU_out, MemtoReg, MemWr, lui_out, auipc);
  Multiplexer #(.select(3), .width(3), .enable("false")) multiplexer_1 (
    .in0(3'b101), .in1(3'b110), .in2(3'b000), .in4(3'b001), .in5(3'b010), .out(multiplexer_1_out),
    .sel(funct3));  // open: in3, in6, in7
  or or_14 (or_14_out, MemtoReg, MemWr);
  or or_15 (\禁用func7 , MemWr, lui_out, auipc, MemtoReg, auipc, auipc, jalr, I_ALU_out);
  and and_10 (jalr, opcode[6], opcode[5], ~opcode[4], ~opcode[3], opcode[2], opcode[1], opcode[0]);  // AND_Gate
  or or_16 (ALUctr[3], or_4_out, multiplexer_2_out);
  Multiplexer #(.enable("false")) multiplexer_2 (
    .in0(funct7[5]), .in1(1'b0), .out(multiplexer_2_out), .sel(\禁用func7_2 ));
  Multiplexer #(.width(3), .enable("false")) multiplexer_3 (
    .in0(3'b000), .in1(multiplexer_1_out), .out(MemOp), .sel(or_14_out));
  and and_11 (Halt, opcode[6], opcode[5], opcode[4], ~opcode[3], ~opcode[2], opcode[1], opcode[0]);  // AND_Gate
  Multiplexer #(.enable("false")) multiplexer_4 (.in0(\禁用func7 ), .in1(1'b0), .out(\禁用func7_2 ), .sel(srli));

  // Other names for the same wires on the sheet: branch = BandJ[2]; jump = ExtOp[2]

  // Notes on the sheet:
  //   输入引脚
  //   请勿修改引脚名称、电路名称及电路封装外观
  //   提示：根据指令种类，把7位指令code用一位指令类型标志位来表示，再通过功能码来区分具体指令，生成控制信号。
  //   输出引脚
endmodule
